# Fritzing sketch Wire-it-all-up (saved by Fritzing 0.7.12b)
perfboards: 2

parts:
  J1 = Screw terminal - 2 pins [package=THT]
  J2 = female pin header, 6 pins [form="♂ (male)" part_number="Bridged Ground"]
  J3 = female pin header, 2 pins [form="♂ (male)"]
  J4 = female pin header, 2 pins [form="♀ (female)"]
  Arduino1 = Arduino Mega
  Q1 = npn-Powertransistor [part_number=TIP120 package="TO220 [THT]"]
  K1 = Relay [part_number=FRS1B-S package=THT]
  U1 = Voltage Regulator - 3.3V [package="TO220 [THT]"]
  R1 = Resistor [tolerance=±5% resistance=1k package=THT]
  D1 = Rectifier Diode [part_number=1N4148 package="300 mil [THT]"]
  Power_plug1 = Power plug
  LED1 = LED - 5mm [color="Blue (430nm)" part_number="405nm Laser" package="5 mm [THT]"]
  Part4 = EasyDriver_v44
  Part5 = EasyDriver_v44
  Part6 = EasyDriver_v44
  J30 = Screw terminal - 2 pins [package=THT]
  J31 = female pin header, 7 pins [form="♀ (female)"]
  J32 = female pin header, 2 pins [form="♀ (female)"]
  J33 = female pin header, 2 pins [form="♀ (female)"]
  J34 = female pin header, 2 pins [form="♀ (female)"]
  J35 = female pin header, 2 pins [form="♀ (female)"]
  J36 = female pin header, 2 pins [form="♀ (female)"]
  J37 = female pin header, 2 pins [form="♀ (female)"]
  S1 = Pushbutton [package=THT]
  S2 = Pushbutton [package=THT]
  S3 = Pushbutton [package=THT]
  S4 = Pushbutton [package=THT]
  S5 = Pushbutton [package=THT]
  S6 = Pushbutton [package=THT]

nets:
  N1: J1.pin1, K1.COIL2, U1.output_voltage, D1.cathode, Power_plug1.VCC
  N2: J1.pin2, J2.pin1, Q1.emitter, K1.C1, K1.C2, U1.input_voltage, Power_plug1.GND, S1.leg1
  N3: J2.pin2, S2.leg1
  N4: J2.pin3, S3.leg1
  N5: J2.pin4, S4.leg1
  N6: J2.pin5, S5.leg1
  N7: J2.pin6, S6.leg1
  N8: J3.pin1, Arduino1.D23, R1.Pin_0
  GND: J3.pin2, Arduino1.GND, Part4.GND, Part5.GND, Part6.GND, J30.pin2, J31.pin1, J32.pin2, J33.pin2, J34.pin2, J35.pin2, J36.pin1, J37.pin1
  N9: J4.pin1, K1.B, LED1.cathode
  N10: J4.pin2, U1.GND, LED1.anode
  N11: Arduino1.D7, Part6.STEP, J31.pin2
  N12: Arduino1.D6, Part6.DIR, J31.pin3
  N13: Arduino1.D5, Part5.STEP, J31.pin4
  N14: Arduino1.D4, Part5.DIR, J31.pin5
  N15: Arduino1.D3, Part4.STEP, J31.pin6
  N16: Arduino1.D2, Part4.DIR, J31.pin7
  N17: Arduino1.D27, S1.leg0
  N18: Arduino1.D29, S2.leg0
  N19: Arduino1.D31, S3.leg0
  N20: Arduino1.D33, S4.leg0
  N21: Arduino1.D35, S5.leg0
  N22: Arduino1.D37, S6.leg0
  N23: Q1.base, R1.Pin_1
  N24: Q1.collector, K1.COIL1, D1.anode
  N25: Part4.V+, Part5.V+, Part6.V+, J30.pin1
  N26: Part4.MS1, J32.pin1
  N27: Part4.MS2, J33.pin1
  N28: Part5.MS1, J35.pin1
  N29: Part5.MS2, J34.pin1
  N30: Part6.MS1, J37.pin2
  N31: Part6.MS2, J36.pin2
